# Fritzing sketch Basic_ControllerForTurntableAndIRCamerashutter (saved by Fritzing 0.9.3b)
breadboards: 1

parts:
  Bauteil1 = EasyDriver_v44
  Bauteil3 = Arduino Uno (Rev3)
  J1 = Piezo Speaker
  Power_plug1 = Power plug
  M1 = Stepper Motor - Bipolar  # not connected
  R1 = Resistor [tolerance=±5% resistance=220 package=THT]
  LED1 = LED - 5mm [color="Infrared (940nm)" package="5 mm [THT]"]
  S1 = Pushbutton [package="[THT]"]
  R2 = Resistor [tolerance=±5% resistance=10k package=THT]
  R3 = Resistor [tolerance=±5% resistance=220 package=THT]
  LED2 = LED - 5mm [color="Blue (505nm)" package="5 mm [THT]"]

nets:
  GND: Bauteil1.GND, Bauteil3.GND, J1.pin1, Power_plug1.GND, LED1.cathode, R2.Pin_1, LED2.cathode
  N1: Bauteil1.V+, Power_plug1.VCC
  N2: Bauteil1.STEP, Bauteil3.D3_PWM
  N3: Bauteil1.DIR, Bauteil3.D2
  N4: Bauteil3.D9_PWM, J1.pin2
  N5: Bauteil3.D12/MISO, R1.Pin_1
  N6: Bauteil3.D13/SCK, R3.Pin_1
  N7: Bauteil3.D4, S1.Pin_1, S1.Pin_2, R2.Pin_0
  N8: Bauteil3.5V, S1.Pin_3, S1.Pin_4
  N9: R1.Pin_0, LED1.anode
  N10: R3.Pin_0, LED2.anode

notes:
  Basic Controller for Steppermotor Turntable and IR Camera Shutter.
  www.fluxgarage.com

// code stored in the sketch: Untitled2.ino
/**
   * FluxGarage - controller for automated turntable with stepper motor and IR camera shutter. 
   * Please note the third party licenses of the included libraries and code snippets, e.g. the "arduino Nikon IR remote" from Aurelien ANTOINE (see below).
   * For more information visit www.fluxgarage.com
**/


// include the display shield library code:
#include <Wire.h>
#include <Adafruit_RGBLCDShield.h>
#include <utility/Adafruit_MCP23017.h>

// The Display + Keypad shield uses the I2C SCL and SDA pins. On classic Arduinos
// this is Analog 4 and 5 so you can't use those for analogRead() anymore
// However, you can connect other I2C sensors to the I2C bus and share
// the I2C bus.
Adafruit_RGBLCDShield lcd = Adafruit_RGBLCDShield();

// These #defines make it easy to set the backlight color
#define RED 0x1
#define YELLOW 0x3
#define GREEN 0x2
#define TEAL 0x6
#define BLUE 0x4
#define VIOLET 0x5
#define WHITE 0x7

//Stepper Pins
#define DIR_PIN 2
#define STEP_PIN 3

// Piezo Sound Pin
#define PIEZOPIN 9


/**
   * arduino Nikon IR remote
   * @license Creative commons: Attribution-Noncommercial-Share Alike 3.0 (http://creativecommons.org/licenses/by-nc-sa/3.0/)
   * @author Aurelien ANTOINE
   * version 1
   * date 20081217
  **/

//Camera Pins
  #define PIN_STATUS 13
  #define PIN_IR_LED 12
  #define FREQ 38400  // IR frequence
   
  //shutter sequence (on,off,on,off ... in microsecond)
  unsigned long sequence[] = {2000,27830,390,1580,410,3580,400,63200,2000,27830,390,1580,410,3580,400,0};
  int seq_l;
   
  //oscd is a delay in microsecond used at each oscillation.
  int oscd;
   
  void oscillate(int pin, unsigned long n, int shine){
    int ir_status=0;
    while(n>0){
      n--;
      delayMicroseconds(oscd);
      ir_status  =  !ir_status; 
      digitalWrite(pin,  ir_status && shine);  
    }
  }
   
  void snap(){
    int i;
    digitalWrite(PIN_STATUS,  1);  
    for(i=0;i<seq_l;i++){
      oscillate(PIN_IR_LED, sequence[i], i%2==0);
    }
    digitalWrite(PIN_STATUS,  0);
  }


// Performance status for stop button
int performstatus = 0;

// Menu variables
int column = 0;
int columnspread = 4; // defining the space between the characters
int columnshift = 1; // shifting the Menu to the right (shifting to the left with negative values)

int valueArray[] = {0, 4, 1, 1};
int valueContraints[] = {3, 4, 4, 1};

// Menu shortcuts
char* menunames[] = {"ST","SP","DE","LI"};

// Real Values 
int realvalues[4][5] = {
{10, 20, 40, 80},
{1, 2, 3, 4, 5},
{0, 5, 10, 25, 50},
{0, 1},
};

// custom FluxGarage logo sign
byte fluxlogo[8] = {
  B00000,
  B00100,
  B00100,
  B00100,
  B01010,
  B10001,
  B00000,
};


void setup() {
  // Debugging output
  Serial.begin(9600);
  
    // Stepper Pins
  pinMode(DIR_PIN, OUTPUT); 
  pinMode(STEP_PIN, OUTPUT); 
   
  // Piezo Sound Pin
  pinMode(PIEZOPIN, OUTPUT);
  
  // set up the LCD's number of columns and rows: 
  lcd.begin(16, 2);
  // set up the LCD's background-color
  lcd.setBacklight(WHITE);

  // Displaying welcome-message
  lcd.createChar(0, fluxlogo);
  lcd.setCursor(2,0);
  lcd.write(byte(0));
  lcd.print(" FluxGarage");
  lcd.setCursor(3,1);
  lcd.print("loading...");
  
  // Initializing camera trigger 
      int min=1, max=100, i;
    int last_oscd=0;
    unsigned long before, intervalle;
    oscd=max;
   
    seq_l = sizeof(sequence)/sizeof(unsigned long);
   
    pinMode(PIN_STATUS, OUTPUT);
    pinMode(PIN_IR_LED, OUTPUT);
    Serial.begin(28800);
   
    //this "while" will process the best "oscd"
    Serial.println("Ready");
    while(last_oscd!=oscd){
      last_oscd=oscd;
      oscd=(min+max)>>1;
   
      before=millis();
      oscillate(PIN_STATUS, FREQ, 1);
      intervalle=millis()-before;
   
      if(intervalle >= 1000) max=oscd;
      else min=oscd;
   
      Serial.print(intervalle);
      Serial.print(" : ");
      Serial.print(min);
      Serial.print("<->");
      Serial.println(max);
    }
   
    Serial.print("oscd: ");
    Serial.println(oscd);
   
    //rewrite the sequence array, we replace all values in microsecond by the number of oscillation
    for(i=0;i<seq_l;i++){
      Serial.print(sequence[i]);
      Serial.print("->");
      sequence[i] = (sequence[i] * FREQ) / (intervalle * 1000);
      Serial.println(sequence[i]);
    }

  // displays complete menu value array after initialisation
  initialprint();

}
 

uint8_t i=0;


void loop() {
uint8_t buttons = lcd.readButtons();
if (buttons) {
    
    if (buttons & BUTTON_UP) {
      if (valueArray[column]<valueContraints[column]){valueArray[column]++;} else {valueArray[column]=0;}
    }
    if (buttons & BUTTON_DOWN) {
     if (valueArray[column]>0){valueArray[column]--;} else {valueArray[column]=valueContraints[column];}
    }
    if (buttons & BUTTON_LEFT) {
      if (column>0){column--;} else {column=3;}
      lcd.setCursor(column*columnspread+columnshift, 0);
    }
    if (buttons & BUTTON_RIGHT) {
      if (column<3){column++;} else {column=0;}
      lcd.setCursor(column*columnspread+columnshift, 0);
      performstatus=0;
    }
    if (buttons & BUTTON_SELECT) {
      performstatus=1; perform();
    }    
    
    // Printing column value from array
    lcd.setCursor(column*columnspread+columnshift, 1);
    lcd.print(realvalues[column][valueArray[column]]);
    lcd.print(" "); // insert blank
    lcd.setCursor(column*columnspread+columnshift, 1); //set cursor back to the right column
    
    // delay for button debouncing
    delay(200);
  }
  
}


// FUNCTIONS //


// Displays complete menu value array
void initialprint () {
  lcd.clear();
  // Printing var column initially
  /* lcd.setCursor(column*columnspread+columnshift, 0);
  // lcd.print(column);
    // lcd.print(menunames[column]); */
    for (column=0;column<4;column++) {
    lcd.setCursor(column*columnspread+columnshift, 0);
    lcd.print(menunames[column]);
  }

  // Printing all values at once initially
  for (column=0;column<4;column++) {
    lcd.setCursor(column*columnspread+columnshift, 1);
    //lcd.print(valueArray[column]);
    lcd.print(realvalues[column][valueArray[column]]);
  }
  // Setting var column back to 0
  column = 0;
  lcd.setCursor(column*columnspread+columnshift, 1); //set cursor back to the right column
  
  // Printing size of steprange values inside of the array
  /*lcd.setCursor(14, 1);
  lcd.print(sizeof(steprange)/2);*/
  
  // Activate cursor 
  lcd.cursor(); //  visible cursor
  //lcd.blink(); // blinking cursor
}

// Performing Photoshoot
void perform () {
  
    // Play confirmation sound
    selectsound();
    
    // turn off light, if defined in the menu
    if (valueArray[3]==0){lcd.setBacklight(LOW);}
    
    // progress information
    lcd.clear();
    lcd.noCursor(); // hide cursor
    lcd.setCursor(0,0);
    lcd.print("Performing");
    lcd.setCursor(0,1);
    lcd.print("Step"); //status information, will be continued in the for loop
    
    // translating variables
    int shootingsteps = realvalues[0][valueArray[0]]; // mumber of steps
    float shootingspeed = realvalues[1][valueArray[1]]*0.01; // rotation speed
    int shootingdelay = realvalues[2][valueArray[2]]*100; // break between each rotation
    
    //rotate a specific number of microsteps (8 microsteps per step)
    //a 200 step stepper would take 1600 micro steps for one full revolution    
    for(int a=0;a<shootingsteps;a++){
      if (performstatus==1) {
      lcd.setCursor(5,1);
      lcd.print(a+1);
      lcd.print(" of ");
      lcd.print(shootingsteps);
      // play sound, take picture
      //selectsound();
      snap();
      delay(shootingdelay);
      // Teller drehen
      rotateDeg(360/shootingsteps, shootingspeed);
      lcd.setCursor(0,0);
      lcd.print("Waiting...");
      delay(shootingdelay);
      lcd.setCursor(0,0);
      lcd.print("Performing");
      askbutton(); // ask, if selectbutton is activated and performstatus has changed
      // if (a==5){performstatus=0;}
      }
      else {break;}
    }
    
    // Clear display, print menu values, activate cursor
    initialprint();
    lcd.cursor();
    
    // turn display light on
    lcd.setBacklight(HIGH);
    lcd.setBacklight(WHITE);
    
    delay(1000);
}



// Button sound
void buttonsound () {
    playTone(5, 50);
}

// Confirmation sound
void selectsound () {
    playTone(10, 1200);
    delay(50);
    playTone(20, 1500);    
}

// Function that generates the sounds
// duration in mSecs, frequency in hertz
void playTone(long duration, int freq) {
    duration *= 1000;
    int period = (1.0 / freq) * 1000000;
    long elapsed_time = 0;
    while (elapsed_time < duration) {
        digitalWrite(PIEZOPIN,HIGH);
        delayMicroseconds(period / 2);
        digitalWrite(PIEZOPIN, LOW);
        delayMicroseconds(period / 2);
        elapsed_time += (period);
    }
}

void rotate(int steps, float speed){ 
  //rotate a specific number of microsteps (8 microsteps per step) - (negative for reverse movement)
  //speed is any number from .01 -> 1 with 1 being fastest - Slower is stronger
  int dir = (steps > 0)? HIGH:LOW;
  steps = abs(steps);

  digitalWrite(DIR_PIN,dir); 

  float usDelay = (1/speed) * 70;

  for(int i=0; i < steps; i++){ 
    digitalWrite(STEP_PIN, HIGH); 
    delayMicroseconds(usDelay); 

    digitalWrite(STEP_PIN, LOW); 
    delayMicroseconds(usDelay); 
  } 
} 

void rotateDeg(float deg, float speed){ 
  //rotate a specific number of degrees (negative for reverse movement)
  //speed is any number from .01 -> 1 with 1 being fastest - Slower is stronger
  int dir = (deg > 0)? HIGH:LOW;
  digitalWrite(DIR_PIN,dir); 

  int steps = abs(deg)*(1/0.225);
  float usDelay = (1/speed) * 70;

  for(int i=0; i < steps; i++){ 
    digitalWrite(STEP_PIN, HIGH); 
    delayMicroseconds(usDelay); 

    digitalWrite(STEP_PIN, LOW); 
    delayMicroseconds(usDelay); 
  } 
}


void askbutton () {
  uint8_t i=0;
  uint8_t buttons = lcd.readButtons();

  if (buttons) {
    if (buttons & BUTTON_SELECT) {
      performstatus=0;
    }    
  }
}
